// Logisim project 15. Circuito otimizado pelo mapa de Karnaugh.circ as structural Verilog: 1 circuit, main circuit main
module main (
  input  A,
  input  B,
  input  C,
  input  D,
  output Sa,
  output Sb,
  output Sc,
  output Sd
);

  wire not_1_out, not_2_out, not_3_out, not_4_out, not_5_out, not_6_out;

  not not_1 (not_1_out, A);
  not not_2 (not_2_out, A);
  not not_3 (not_3_out, B);
  not not_4 (not_4_out, A);
  not not_5 (not_5_out, B);
  not not_6 (not_6_out, C);
  and and_1 (Sb, not_1_out, B);
  and and_2 (Sc, not_2_out, not_3_out, C);
  and and_3 (Sd, not_4_out, not_5_out, not_6_out, D);

  assign Sa = A;

  // Notes on the sheet:
  //   Otimização de circuitos pelo mapa de Karnaugh
endmodule
