// Logisim project 17. Detector de número primo.circ as structural Verilog: 1 circuit, main circuit main
module main (
  input  A,
  input  B,
  input  C,
  input  D,
  output S
);

  wire and_1_out, and_2_out, and_3_out, and_4_out, not_1_out, not_2_out, not_3_out, not_4_out, not_5_out;

  not not_1 (not_1_out, A);
  not not_2 (not_2_out, B);
  not not_3 (not_3_out, B);
  not not_4 (not_4_out, A);
  not not_5 (not_5_out, C);
  and and_1 (and_1_out, not_1_out, not_2_out, C);
  and and_2 (and_2_out, not_3_out, C, D);
  and and_3 (and_3_out, not_4_out, B, D);
  and and_4 (and_4_out, B, not_5_out, D);
  or or_1 (S, and_1_out, and_2_out, and_3_out, and_4_out);

  // Notes on the sheet:
  //   Detector de número primo
endmodule
