// Logisim project Flip-Flop D.circ as structural Verilog: 2 circuits, main circuit main
module main (
  input  in_1,
  output out_2,
  output out_3
);

  wire clock_1_out;

  Clock clock_1 (.out(clock_1_out));
  FLIP_FLOP_D flip_flop_d_1 (.D(in_1), .Q(out_2), .minus_Q(out_3), .CLOCK(clock_1_out));
endmodule

module FLIP_FLOP_D (
  input  D,
  input  CLOCK,
  output Q,
  output minus_Q
);

  wire nand_1_out, nand_2_out, nand_3_out, nand_4_out, nand_5_out, nand_6_out, not_1_out, not_2_out;

  not not_1 (not_1_out, CLOCK);
  nand nand_1 (nand_1_out, D, not_1_out);
  nand nand_2 (nand_2_out, nand_1_out, not_1_out);
  not not_2 (not_2_out, not_1_out);
  nand nand_3 (nand_3_out, nand_1_out, nand_4_out);
  nand nand_4 (nand_4_out, nand_3_out, nand_2_out);
  nand nand_5 (nand_5_out, nand_3_out, not_2_out);
  nand nand_6 (nand_6_out, nand_5_out, not_2_out);
  nand nand_7 (Q, nand_5_out, minus_Q);
  nand nand_8 (minus_Q, Q, nand_6_out);
endmodule
