// Logisim project MUX de 4 entradas.circ as structural Verilog: 1 circuit, main circuit main
module main (
  input  S0,
  input  W0,
  input  S1,
  input  W1,
  input  W2,
  input  W3,
  output f
);

  wire and_1_out, and_2_out, and_3_out, and_4_out, not_1_out, not_2_out;

  not not_1 (not_1_out, S0);
  not not_2 (not_2_out, S1);
  and and_1 (and_1_out, not_1_out, W0, not_2_out);
  and and_2 (and_2_out, S0, W1, not_2_out);
  and and_3 (and_3_out, not_2_out, W2, S1);
  and and_4 (and_4_out, S0, W3, S1);
  or or_1 (f, and_1_out, and_2_out, and_3_out, and_4_out);
endmodule
