// Logisim project extensor de 4 para 8.circ as structural Verilog: 2 circuits, main circuit main
module main (
  input  [3:0] in_1,
  output [7:0] out_2
);

  extensor_4_para_8 extensor_4_para_8_1 (.in_1(in_1), .out_2(out_2));
endmodule

module extensor_4_para_8 (
  input  [3:0] in_1,
  output [7:0] out_2
);


  assign out_2 = {{5{in_1[3]}}, in_1[2:0]};
endmodule
