// Logisim project registrador de 8 bits.circ as structural Verilog
module circuito_1_bit (
  input  s,
  input  e,
  output q
);

  wire nand_1_out, nand_2_out, nand_4_out;

  nand nand_1 (nand_1_out, s, e);
  nand nand_2 (nand_2_out, nand_1_out, e);
  nand nand_3 (q, nand_1_out, nand_4_out);
  nand nand_4 (nand_4_out, q, nand_2_out);
endmodule

module circuito_8_bits (
  input  [7:0] in,
  input  ativador,
  output [7:0] out
);

  circuito_1_bit circuito_1_bit_1 (.s(in[0]), .e(ativador), .q(out[0]));
  circuito_1_bit circuito_1_bit_2 (.s(in[1]), .e(ativador), .q(out[1]));
  circuito_1_bit circuito_1_bit_3 (.s(in[2]), .e(ativador), .q(out[2]));
  circuito_1_bit circuito_1_bit_4 (.s(in[3]), .e(ativador), .q(out[3]));
  circuito_1_bit circuito_1_bit_5 (.s(in[4]), .e(ativador), .q(out[4]));
  circuito_1_bit circuito_1_bit_6 (.s(in[5]), .e(ativador), .q(out[5]));
  circuito_1_bit circuito_1_bit_7 (.s(in[6]), .e(ativador), .q(out[6]));
  circuito_1_bit circuito_1_bit_8 (.s(in[7]), .e(ativador), .q(out[7]));
endmodule

module registrador_de_8_bits (
  input  [7:0] in,
  input  ativador,
  output [7:0] out
);

  and and_1 (out[0], in[0], ativador);
  and and_2 (out[1], in[1], ativador);
  and and_3 (out[2], in[2], ativador);
  and and_4 (out[3], in[3], ativador);
  and and_5 (out[4], in[4], ativador);
  and and_6 (out[5], in[5], ativador);
  and and_7 (out[6], in[6], ativador);
  and and_8 (out[7], in[7], ativador);
endmodule

module CPU_ENABLE (
  input  [7:0] prim__in,
  input  set1,
  input  set2,
  output [7:0] Regist,
  output [7:0] out_5
);

  circuito_8_bits circuito_8_bits_1 (.in(prim__in), .ativador(set1), .out(Regist));
  registrador_de_8_bits registrador_de_8_bits_1 (.in(Regist), .ativador(set2), .out(out_5));
endmodule
