// Logisim project somadorde8bits.circ as structural Verilog
module somador_de_1_bit (
  input  a0,
  input  a1,
  input  cin,
  output s,
  output cout
);

  wire and_1_out, and_2_out, and_3_out, xor_1_out;

  and and_1 (and_1_out, a0, a1);
  and and_2 (and_2_out, a0, cin);
  and and_3 (and_3_out, a1, cin);
  xor xor_1 (xor_1_out, a0, a1);
  or or_1 (cout, and_1_out, and_2_out, and_3_out);
  xor xor_2 (s, xor_1_out, cin);
endmodule

module somador_de_4_bits (
  input  b3,
  input  a3,
  input  b2,
  input  a2,
  input  b1,
  input  a1,
  input  b0,
  input  a0,
  input  cin,
  output cout,
  output c3,
  output c2,
  output c1,
  output c0
);

  wire somador_de_1_bit_2_cout, somador_de_1_bit_3_cout, somador_de_1_bit_4_cout;

  somador_de_1_bit somador_de_1_bit_1 (.a0(a3), .a1(b3), .cin(somador_de_1_bit_2_cout), .s(c3), .cout(cout));
  somador_de_1_bit somador_de_1_bit_2 (
    .a0(a2), .a1(b2), .cin(somador_de_1_bit_3_cout), .s(c2), .cout(somador_de_1_bit_2_cout));
  somador_de_1_bit somador_de_1_bit_3 (
    .a0(a1), .a1(b1), .cin(somador_de_1_bit_4_cout), .s(c1), .cout(somador_de_1_bit_3_cout));
  somador_de_1_bit somador_de_1_bit_4 (.a0(a0), .a1(b0), .cin(cin), .s(c0), .cout(somador_de_1_bit_4_cout));
endmodule

module somador_de_8_bits (
  input  a7,
  input  a6,
  input  a5,
  input  a4,
  input  a3,
  input  a2,
  input  a1,
  input  a0,
  input  cin,
  input  b7,
  input  b6,
  input  b5,
  input  b4,
  input  b3,
  input  b2,
  input  b1,
  input  b0,
  output overflow,
  output S7,
  output S6,
  output S5,
  output S4,
  output S3,
  output S2,
  output S1,
  output S0
);

  wire somador_de_4_bits_2_cout;

  somador_de_4_bits somador_de_4_bits_1 (
    .b3(b7), .a3(a7), .b2(b6), .a2(a6), .b1(b5), .a1(a5), .b0(b4), .a0(a4), .cout(overflow), .c3(S7),
    .c2(S6), .c1(S5), .c0(S4), .cin(somador_de_4_bits_2_cout));
  somador_de_4_bits somador_de_4_bits_2 (
    .b3(b3), .a3(a3), .b2(b2), .a2(a2), .b1(b1), .a1(a1), .b0(b0), .a0(a0), .cout(somador_de_4_bits_2_cout),
    .c3(S3), .c2(S2), .c1(S1), .c0(S0), .cin(cin));
endmodule

module somador_8_bits___4 (
  input  a7,
  input  a6,
  input  a5,
  input  a4,
  input  a3,
  input  a2,
  input  a1,
  input  a0,
  input  cin,
  output overflow,
  output out_11,
  output out_12,
  output out_13,
  output out_14,
  output out_15,
  output out_16,
  output out_17,
  output out_18
);

  somador_de_8_bits somador_de_8_bits_1 (
    .b0(1'b0), .a0(a0), .b1(1'b0), .a1(a1), .b2(1'b1), .a2(a2), .S7(out_11), .S3(out_15), .b3(1'b0), .a3(a3),
    .S6(out_12), .S2(out_16), .b4(1'b0), .a4(a4), .S5(out_13), .S1(out_17), .b5(1'b0), .a5(a5), .S4(out_14),
    .S0(out_18), .b6(1'b0), .a6(a6), .b7(1'b0), .a7(a7), .overflow(overflow), .cin(cin));
endmodule
